# Fritzing sketch controlRGBByPhotoresistor (saved by Fritzing 0.9.2b)

parts:
  元件1 = Adeept Uno (Rev3)
  Part1 = Adeept Photoresistor Module [part_number="Adeept Photoresistor Module"]
  Part2 = Adeept Breadboard [part_number="Adeept Breadboard"]
  Part3 = Adeept RGB LED Module [part_number="Adeept RGB LED Module"]

nets:
  N1: 元件1.A0, Part1.A
  N2: 元件1.D10_PWM/SS, Part3.G
  N3: 元件1.D11_PWM/MOSI, Part3.R
  N4: 元件1.D6_PWM, Part3.B
  N5: 元件1.5V, Part1.+, Part2.pin_185, Part2.pin_187, Part2.pin_189, Part3.+
  N6: 元件1.GND, Part1.-

custom parts:
  Adeept Uno (Rev3): The Adeept Uno is a microcontroller board based on the ATmega328 (datasheet). It has 14 digital input/output pins (of which 6 can be used as PWM outputs), 6 analog inputs, a 16 MHz ceramic resonator, a USB connection, a power jack, an ICSP header, and a reset button. It contains everything needed to support the microcontroller; simply connect it to a computer with a USB cable or power it with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
