# Fritzing sketch AdeeptMQ2LCD12864Alarm (saved by Fritzing 0.9.2b)

parts:
  元件1 = Adeept Uno (Rev3)
  Part1 = Adeept Breadboard [part_number="Adeept Breadboard"]
  GLCD_128x1 = 128 x 64 Graphic LCD
  Part2 = Adeept MQ-2 Gas Sensor Module [part_number="Adeept MQ-2 Gas Sensor Module"]
  Part3 = Adeept Passive Buzzer Module [part_number="Adeept Passive Buzzer Module"]
  Part4 = Adeept RGB LED Module [part_number="Adeept RGB LED Module"]
  Part5 = Adeept Blue Button Module [part_number="Adeept Blue Button Module"]
  Part6 = Adeept Blue Button Module [part_number="Adeept Blue Button Module"]
  Part7 = Adeept Red Button Module [part_number="Adeept Red Button Module"]
  Part8 = Adeept White Button Module [part_number="Adeept White Button Module"]

nets:
  N1: 元件1.A1, Part2.A
  N2: 元件1.D8, GLCD_128x1.4_D/I
  N3: 元件1.D9_PWM, GLCD_128x1.5_R/W
  N4: 元件1.D10_PWM/SS, Part4.G
  N5: 元件1.D11_PWM/MOSI, Part4.R
  N6: 元件1.D12/MISO, Part6.S
  N7: 元件1.D13/SCK, Part5.S
  N8: 元件1.D0/RX, Part8.S
  N9: 元件1.D1/TX, Part7.S
  N10: 元件1.D3_PWM, GLCD_128x1.6_Enable
  N11: 元件1.D5_PWM, Part3.S
  N12: 元件1.D6_PWM, Part4.B
  N13: 元件1.D7, Part2.S
  N14: 元件1.5V, Part1.pin_155, Part1.pin_156, Part1.pin_157, Part1.pin_158, Part1.pin_159, Part1.pin_175, Part1.pin_176, Part1.pin_177, Part1.pin_178, Part1.pin_179, Part1.pin_180, Part1.pin_181, Part1.pin_182, Part1.pin_184, GLCD_128x1.2_Vdd, GLCD_128x1.19_A(+), Part2.+, Part3.+, Part4.+, Part5.+, Part6.+, Part7.+, Part8.+
  N15: 元件1.GND, Part1.pin_305, Part1.pin_306, Part1.pin_307, Part1.pin_308, Part1.pin_309, Part1.pin_310, Part1.pin_312, Part1.pin_313, Part1.pin_314, Part1.pin_315, Part1.pin_316, Part1.pin_317, Part1.pin_318, Part1.pin_319, GLCD_128x1.1_Vss, GLCD_128x1.15_CS1, GLCD_128x1.20_K(-), Part2.-, Part3.-, Part5.-, Part6.-, Part7.-, Part8.-

custom parts:
  Adeept Uno (Rev3): The Adeept Uno is a microcontroller board based on the ATmega328 (datasheet). It has 14 digital input/output pins (of which 6 can be used as PWM outputs), 6 analog inputs, a 16 MHz ceramic resonator, a USB connection, a power jack, an ICSP header, and a reset button. It contains everything needed to support the microcontroller; simply connect it to a computer with a USB cable or power it with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
