# Fritzing sketch barometerDisplaySerial (saved by Fritzing 0.9.2b)

parts:
  元件1 = Adeept Uno (Rev3)
  Part2 = Adeept Barometer Sensor Module [part_number="Adeept Barometer Sensor Module"]

nets:
  N1: 元件1.A4/SDA, Part2.SDA
  N2: 元件1.A5/SCL, Part2.CLK
  3V3: 元件1.3V3, Part2.3.3V
  N3: 元件1.GND, Part2.-

custom parts:
  Adeept Uno (Rev3): The Adeept Uno is a microcontroller board based on the ATmega328 (datasheet). It has 14 digital input/output pins (of which 6 can be used as PWM outputs), 6 analog inputs, a 16 MHz ceramic resonator, a USB connection, a power jack, an ICSP header, and a reset button. It contains everything needed to support the microcontroller; simply connect it to a computer with a USB cable or power it with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
