# Fritzing sketch buttonDisplayViaProcessing (saved by Fritzing 0.9.2b)

parts:
  元件1 = Adeept Red Button Module [part_number="Adeept Red Button Module"]
  元件2 = Adeept White Button Module [part_number="Adeept White Button Module"]
  元件3 = Adeept Uno (Rev3)
  元件4 = Adeept Breadboard [part_number="Adeept Breadboard"]
  元件5 = Adeept Blue Button Module [part_number="Adeept Blue Button Module"]
  元件6 = Adeept Blue Button Module [part_number="Adeept Blue Button Module"]

nets:
  N1: 元件1.S, 元件3.D2
  N2: 元件1.+, 元件2.+, 元件3.5V, 元件4.pin_100, 元件4.pin_101, 元件4.pin_102, 元件4.pin_103, 元件4.pin_104, 元件5.+, 元件6.+
  N3: 元件1.-, 元件2.-, 元件3.GND, 元件4.pin_235, 元件4.pin_236, 元件4.pin_237, 元件4.pin_238, 元件4.pin_239, 元件5.-, 元件6.-
  N4: 元件2.S, 元件3.D3_PWM
  N5: 元件3.D12/MISO, 元件5.S
  N6: 元件3.D13/SCK, 元件6.S

custom parts:
  Adeept Uno (Rev3): The Adeept Uno is a microcontroller board based on the ATmega328 (datasheet). It has 14 digital input/output pins (of which 6 can be used as PWM outputs), 6 analog inputs, a 16 MHz ceramic resonator, a USB connection, a power jack, an ICSP header, and a reset button. It contains everything needed to support the microcontroller; simply connect it to a computer with a USB cable or power it with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
