# Fritzing sketch AdeeptWeatherBox (saved by Fritzing 0.9.2b)

parts:
  元件1 = Adeept Uno (Rev3)
  Part1 = Adeept Breadboard [part_number="Adeept Breadboard"]
  GLCD_128x1 = 128 x 64 Graphic LCD
  Part2 = Adeept RGB LED Module [part_number="Adeept RGB LED Module"]
  Part3 = Adeept Blue Button Module [part_number="Adeept Blue Button Module"]
  Part4 = Adeept Blue Button Module [part_number="Adeept Blue Button Module"]
  Part5 = Adeept White Button Module [part_number="Adeept White Button Module"]
  Part6 = Adeept Red Button Module [part_number="Adeept Red Button Module"]
  Part7 = Adeept Passive Buzzer Module [part_number="Adeept Passive Buzzer Module"]
  Part8 = Adeept Photoresistor Module [part_number="Adeept Photoresistor Module"]
  Part9 = Adeept DHT-11 Sensor Module [part_number="Adeept DHT-11 Sensor Module"]
  Part10 = Adeept Barometer Sensor Module [part_number="Adeept Barometer Sensor Module"]
  Part11 = Adeept MQ-2 Gas Sensor Module [part_number="Adeept MQ-2 Gas Sensor Module"]
  C1 = Electrolytic Capacitor [capacitance=220µF package="100 mil [THT, electrolytic]"]
  R1 = Resistor [tolerance=±5% resistance=150 package=THT]
  R2 = Resistor [tolerance=±5% resistance=220 package=THT]
  C2 = Electrolytic Capacitor [capacitance=1µF package="100 mil [THT, electrolytic]"]
  R3 = Resistor [tolerance=±5% resistance=220 package=THT]
  C3 = Electrolytic Capacitor [capacitance=1µF package="100 mil [THT, electrolytic]"]

nets:
  N1: 元件1.A0, Part8.A
  N2: 元件1.A1, Part11.A
  N3: 元件1.A4/SDA, Part10.SDA
  N4: 元件1.A5/SCL, Part10.CLK
  N5: 元件1.D8, GLCD_128x1.4_D/I
  N6: 元件1.D9_PWM, GLCD_128x1.5_R/W
  N7: 元件1.D10_PWM/SS, Part2.G
  N8: 元件1.D11_PWM/MOSI, Part2.R
  N9: 元件1.D12/MISO, Part3.S
  N10: 元件1.D13/SCK, Part4.S
  N11: 元件1.D0/RX, Part5.S
  N12: 元件1.D1/TX, Part6.S
  N13: 元件1.D2, Part9.S
  N14: 元件1.D3_PWM, GLCD_128x1.6_Enable
  N15: 元件1.D5_PWM, Part7.S
  N16: 元件1.D6_PWM, Part2.B
  N17: 元件1.D7, Part11.S
  3V3: 元件1.3V3, Part10.3.3V
  N18: 元件1.5V, Part1.pin_115, Part1.pin_116, Part1.pin_117, Part1.pin_118, Part1.pin_119, Part1.pin_135, Part1.pin_136, Part1.pin_137, Part1.pin_138, Part1.pin_139, Part1.pin_160, Part1.pin_161, Part1.pin_163, Part1.pin_164, Part1.pin_175, Part1.pin_176, Part1.pin_177, Part1.pin_178, Part1.pin_179, Part1.pin_180, Part1.pin_181, Part1.pin_182, Part1.pin_184, GLCD_128x1.2_Vdd, GLCD_128x1.19_A(+), Part2.+, Part3.+, Part4.+, Part5.+, Part6.+, Part7.+, Part8.+, Part9.+, Part11.+, C1.+, R1.Pin_0, R2.Pin_0, C2.+, R3.Pin_0, C3.+
  N19: 元件1.GND, Part1.pin_235, Part1.pin_239, Part1.pin_255, Part1.pin_257, Part1.pin_258, Part1.pin_259, Part1.pin_280, Part1.pin_281, Part1.pin_282, Part1.pin_283, Part1.pin_284, Part1.pin_310, Part1.pin_311, Part1.pin_312, Part1.pin_313, Part1.pin_314, Part1.pin_315, Part1.pin_316, Part1.pin_317, Part1.pin_318, Part1.pin_319, GLCD_128x1.1_Vss, GLCD_128x1.15_CS1, GLCD_128x1.20_K(-), Part3.-, Part4.-, Part5.-, Part6.-, Part7.-, Part8.-, Part9.-, Part10.-, Part11.-, C1.-, C2.-, C3.-
  N20: Part1.pin_104, R1.Pin_1, R2.Pin_1, R3.Pin_1

custom parts:
  Adeept Uno (Rev3): The Adeept Uno is a microcontroller board based on the ATmega328 (datasheet). It has 14 digital input/output pins (of which 6 can be used as PWM outputs), 6 analog inputs, a 16 MHz ceramic resonator, a USB connection, a power jack, an ICSP header, and a reset button. It contains everything needed to support the microcontroller; simply connect it to a computer with a USB cable or power it with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
