# Fritzing sketch AdeeptSnakeGame (saved by Fritzing 0.9.2b)

parts:
  元件1 = Adeept Uno (Rev3)
  Part1 = Adeept Breadboard [part_number="Adeept Breadboard"]
  GLCD_128x1 = 128 x 64 Graphic LCD
  Part2 = Adeept Red Button Module [part_number="Adeept Red Button Module"]
  Part3 = Adeept White Button Module [part_number="Adeept White Button Module"]
  Part4 = Adeept Blue Button Module [part_number="Adeept Blue Button Module"]
  Part5 = Adeept Blue Button Module [part_number="Adeept Blue Button Module"]

nets:
  N1: 元件1.A2, GLCD_128x1.5_R/W
  N2: 元件1.A3, GLCD_128x1.4_D/I
  N3: 元件1.A4/SDA, GLCD_128x1.6_Enable
  N4: 元件1.D8, GLCD_128x1.11_DB4
  N5: 元件1.D9_PWM, GLCD_128x1.12_DB5
  N6: 元件1.D10_PWM/SS, GLCD_128x1.13_DB6
  N7: 元件1.D11_PWM/MOSI, GLCD_128x1.14_DB7
  N8: 元件1.D12/MISO, Part5.S
  N9: 元件1.D13/SCK, Part4.S
  N10: 元件1.D0/RX, Part3.S
  N11: 元件1.D1/TX, Part2.S
  N12: 元件1.D4, GLCD_128x1.7_DB0
  N13: 元件1.D5_PWM, GLCD_128x1.8_DB1
  N14: 元件1.D6_PWM, GLCD_128x1.9_BD2
  N15: 元件1.D7, GLCD_128x1.10_DB3
  N16: 元件1.5V, Part1.pin_155, Part1.pin_156, Part1.pin_157, Part1.pin_158, Part1.pin_159, Part1.pin_180, Part1.pin_181, Part1.pin_182, Part1.pin_183, Part1.pin_184, GLCD_128x1.2_Vdd, GLCD_128x1.15_CS1, GLCD_128x1.19_A(+), Part2.+, Part3.+, Part4.+, Part5.+
  N17: 元件1.GND, Part1.pin_290, Part1.pin_292, Part1.pin_293, Part1.pin_294, Part1.pin_315, Part1.pin_316, Part1.pin_317, Part1.pin_318, Part1.pin_319, GLCD_128x1.1_Vss, GLCD_128x1.20_K(-), Part2.-, Part3.-, Part4.-, Part5.-

custom parts:
  Adeept Uno (Rev3): The Adeept Uno is a microcontroller board based on the ATmega328 (datasheet). It has 14 digital input/output pins (of which 6 can be used as PWM outputs), 6 analog inputs, a 16 MHz ceramic resonator, a USB connection, a power jack, an ICSP header, and a reset button. It contains everything needed to support the microcontroller; simply connect it to a computer with a USB cable or power it with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
