# Fritzing sketch controlBuzzerByButton (saved by Fritzing 0.9.2b)

parts:
  元件2 = Adeept White Button Module [part_number="Adeept White Button Module"]
  元件3 = Adeept Uno (Rev3)
  元件4 = Adeept Breadboard [part_number="Adeept Breadboard"]
  元件5 = Adeept Blue Button Module [part_number="Adeept Blue Button Module"]
  元件6 = Adeept Blue Button Module [part_number="Adeept Blue Button Module"]
  元件1 = Adeept Red Button Module [part_number="Adeept Red Button Module"]
  Part1 = Adeept Passive Buzzer Module [part_number="Adeept Passive Buzzer Module"]

nets:
  N1: 元件2.S, 元件3.D0/RX
  N2: 元件2.+, 元件3.5V, 元件4.pin_50, 元件4.pin_51, 元件4.pin_52, 元件4.pin_53, 元件4.pin_54, 元件4.pin_71, 元件4.pin_73, 元件4.pin_74, 元件5.+, 元件6.+, 元件1.+, Part1.+
  N3: 元件2.-, 元件3.GND, 元件4.pin_185, 元件4.pin_186, 元件4.pin_187, 元件4.pin_188, 元件4.pin_189, 元件4.pin_223, 元件4.pin_224, 元件5.-, 元件6.-, 元件1.-, Part1.-
  N4: 元件3.D12/MISO, 元件5.S
  N5: 元件3.D13/SCK, 元件6.S
  N6: 元件3.D1/TX, 元件1.S
  N7: 元件3.D5_PWM, Part1.S

custom parts:
  Adeept Uno (Rev3): The Adeept Uno is a microcontroller board based on the ATmega328 (datasheet). It has 14 digital input/output pins (of which 6 can be used as PWM outputs), 6 analog inputs, a 16 MHz ceramic resonator, a USB connection, a power jack, an ICSP header, and a reset button. It contains everything needed to support the microcontroller; simply connect it to a computer with a USB cable or power it with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
